// Logisim project simon_says_main.circ as structural Verilog: 1 circuit, main circuit main
// 4
module main (
  input  in_1,
  input  in_2
);

  wire and_1_out, and_2_out, and_3_out, and_4_out, and_5_out, and_6_out, and_7_out, and_8_out, and_9_out,
       and_10_out, and_11_out, and_12_out, and_13_out, and_14_out, and_15_out, and_16_out, and_17_out,
       and_18_out, and_19_out, and_20_out, buffer_1_out, buffer_2_out, buffer_3_out, buffer_4_out,
       buffer_5_out, buffer_6_out, buffer_7_out, buffer_8_out, buffer_9_out, buffer_10_out, button_4_out,
       button_5_out, button_7_out, button_8_out, button_9_out, button_10_out, clock_1_out, clock_2_out,
       clock_3_out, clock_4_out, d_ff_1_q, d_ff_2_q, d_ff_3_q, d_ff_4_q, d_ff_5_q, d_ff_6_q, d_ff_7_q,
       d_ff_8_q, d_ff_9_q, d_ff_10_q, d_ff_11_q, d_ff_12_q, d_ff_18_q, d_ff_19_q, d_ff_20_q, d_ff_21_q,
       d_ff_22_q, d_ff_23_q, d_ff_24_q, d_ff_25_q, d_ff_26_q, d_ff_27_q, d_ff_28_q, d_ff_29_q, d_ff_30_q,
       d_ff_31_q, d_ff_32_q, d_ff_33_q, d_ff_34_q, d_ff_35_q, d_ff_36_q, d_ff_37_q, d_ff_38_q, d_ff_39_q,
       d_ff_40_q, d_ff_41_q, d_ff_42_q, d_ff_43_q, d_ff_44_q, d_ff_45_q, d_ff_46_q, d_ff_47_q, d_ff_48_q,
       d_ff_49_q, d_ff_50_q, decoder_1_out0, decoder_1_out1, decoder_1_out2, decoder_1_out3, decoder_1_out4,
       decoder_1_out5, decoder_1_out6, decoder_1_out7, demultiplexer_1_out0, demultiplexer_1_out1,
       demultiplexer_1_out2, demultiplexer_1_out3, demultiplexer_2_out0, demultiplexer_2_out1,
       demultiplexer_2_out2, demultiplexer_2_out3, demultiplexer_3_out0, demultiplexer_3_out1,
       demultiplexer_3_out2, demultiplexer_3_out3, demultiplexer_4_out0, demultiplexer_4_out1,
       demultiplexer_4_out2, demultiplexer_4_out3, demultiplexer_5_out0, demultiplexer_5_out1,
       demultiplexer_5_out2, demultiplexer_5_out3, demultiplexer_6_out0, demultiplexer_6_out1,
       demultiplexer_6_out2, demultiplexer_6_out3, demultiplexer_7_out0, demultiplexer_7_out1,
       demultiplexer_7_out2, demultiplexer_7_out3, demultiplexer_8_out0, demultiplexer_8_out1,
       demultiplexer_8_out2, demultiplexer_8_out3, demultiplexer_9_out0, demultiplexer_9_out1,
       demultiplexer_9_out2, demultiplexer_9_out3, demultiplexer_9_out4, demultiplexer_9_out5,
       demultiplexer_9_out6, demultiplexer_9_out7, dipswitch_1_p1, dipswitch_1_p2, dipswitch_1_p3,
       dipswitch_1_p4, dipswitch_2_p1, dipswitch_2_p2, dipswitch_2_p3, dipswitch_2_p4, dipswitch_3_p1,
       dipswitch_3_p2, dipswitch_3_p3, dipswitch_3_p4, dipswitch_3_p5, dipswitch_3_p6, j_k_ff_1_qn,
       j_k_ff_2_qn, j_k_ff_3_qn, j_k_ff_4_qn, j_k_ff_5_q, j_k_ff_8_qn, j_k_ff_9_qn, j_k_ff_10_qn,
       j_k_ff_11_qn, multiplexer_1_out, multiplexer_2_out, multiplexer_3_out, multiplexer_4_out,
       multiplexer_5_out, multiplexer_6_out, multiplexer_7_out, multiplexer_8_out, multiplexer_9_out,
       multiplexer_10_out, multiplexer_11_out, multiplexer_12_out, multiplexer_13_out, not_1_out, not_2_out,
       not_3_out, not_4_out, not_5_out, not_6_out, not_7_out, or_1_out, or_2_out, or_3_out, or_4_out,
       or_5_out, or_6_out, or_7_out, or_8_out, or_9_out, or_10_out, or_11_out, or_12_out, or_13_out,
       or_14_out, or_15_out, or_16_out, or_17_out, or_18_out, register_1_q, register_2_q, register_3_q,
       register_4_q, register_5_q, register_6_q, register_7_q, register_8_q, xnor_1_out, xnor_2_out,
       xnor_3_out, xnor_4_out, xnor_5_out, xnor_6_out, xnor_7_out;
  wire [1:0] random_1_out;
  wire [2:0] d_ff_13_q, j_k_ff_1_q, j_k_ff_2_q, j_k_ff_8_q, j_k_ff_9_q;

  Clock clock_1 (.out(clock_1_out));
  Clock clock_2 (.out(clock_2_out));
  Clock clock_3 (.out(clock_3_out));
  D_Flip_Flop d_ff_1 (.D(j_k_ff_5_q), .clk(j_k_ff_5_q), .Q(d_ff_1_q), .reset(and_4_out));  // open: Qn, preset
  Register #(.width(1)) register_1 (.D(dipswitch_1_p1), .en(1'b1), .clk(clock_1_out), .Q(register_1_q), .clr(1'b0));
  Register #(.width(1)) register_2 (.D(dipswitch_2_p1), .en(1'b1), .clk(clock_2_out), .Q(register_2_q), .clr(1'b0));
  not not_1 (not_1_out, d_ff_2_q);
  D_Flip_Flop d_ff_2 (.D(or_3_out), .clk(or_3_out), .Q(d_ff_2_q), .reset(and_4_out));  // open: Qn, preset
  and and_1 (and_1_out, d_ff_1_q, clock_4_out);
  or or_1 (or_1_out, or_3_out, button_9_out);
  and and_2 (and_2_out, d_ff_2_q, and_1_out);
  and and_3 (and_3_out, and_2_out, not_3_out);
  Clock clock_4 (.out(clock_4_out));
  // DipSwitch #(.number(4)) dipswitch_1: pin names not known; wires that end beside it: dipswitch_1_p1, dipswitch_1_p2, dipswitch_1_p3, dipswitch_1_p4
  // DipSwitch #(.number(4)) dipswitch_2: pin names not known; wires that end beside it: dipswitch_2_p1, dipswitch_2_p2, dipswitch_2_p3, dipswitch_2_p4
  J_K_Flip_Flop j_k_ff_1 (
    .J(in_1), .K(in_1), .clk(clock_3_out), .Q(j_k_ff_1_q[0]), .Qn(j_k_ff_1_qn));  // open: preset, reset
  D_Flip_Flop d_ff_3 (.D(and_6_out), .clk(and_6_out), .Q(d_ff_3_q), .reset(or_2_out));  // open: Qn, preset
  J_K_Flip_Flop j_k_ff_2 (
    .J(and_2_out), .K(and_2_out), .clk(and_2_out), .Q(j_k_ff_2_q[0]), .Qn(j_k_ff_2_qn), .preset(or_3_out),
    .reset(and_4_out));
  D_Flip_Flop d_ff_4 (.D(and_3_out), .clk(and_3_out), .Q(d_ff_4_q), .reset(and_4_out));  // open: Qn, preset
  D_Flip_Flop d_ff_5 (.D(or_1_out), .clk(or_1_out), .Q(d_ff_5_q), .reset(and_4_out));  // open: Qn, preset
  Register #(.width(1)) register_3 (.D(dipswitch_1_p2), .en(1'b1), .clk(clock_1_out), .Q(register_3_q), .clr(1'b0));
  xnor xnor_1 (xnor_1_out, register_1_q, register_2_q);
  Register #(.width(1)) register_4 (.D(dipswitch_2_p2), .en(1'b1), .clk(clock_2_out), .Q(register_4_q), .clr(1'b0));
  J_K_Flip_Flop j_k_ff_3 (
    .J(in_1), .K(in_1), .clk(j_k_ff_1_qn), .Q(j_k_ff_1_q[1]), .Qn(j_k_ff_3_qn));  // open: preset, reset
  D_Flip_Flop #(.trigger("falling")) d_ff_6 (
    .D(d_ff_3_q), .clk(and_6_out), .Q(d_ff_6_q), .reset(not_2_out));  // open: Qn, preset
  J_K_Flip_Flop j_k_ff_4 (
    .J(and_2_out), .K(and_2_out), .clk(j_k_ff_2_qn), .Q(j_k_ff_2_q[1]), .Qn(j_k_ff_4_qn), .preset(or_3_out),
    .reset(and_4_out));
  D_Flip_Flop #(.trigger("falling")) d_ff_7 (
    .D(d_ff_4_q), .clk(and_3_out), .Q(d_ff_7_q), .reset(and_4_out));  // open: Qn, preset
  J_K_Flip_Flop #(.trigger("falling")) j_k_ff_5 (
    .J(d_ff_5_q), .K(d_ff_5_q), .clk(clock_4_out), .Q(j_k_ff_5_q), .reset(and_4_out));  // open: Qn, preset
  LED led_1 (.in(j_k_ff_1_q[2]));
  LED led_2 (.in(j_k_ff_1_q[1]));
  LED led_3 (.in(j_k_ff_1_q[0]));
  or or_2 (or_2_out, d_ff_6_q, button_10_out);
  not not_2 (not_2_out, d_ff_3_q);
  or or_3 (or_3_out, d_ff_3_q, button_9_out);
  J_K_Flip_Flop j_k_ff_6 (
    .J(and_2_out), .K(and_2_out), .clk(j_k_ff_4_qn), .Q(j_k_ff_2_q[2]), .preset(or_3_out), .reset(and_4_out));  // open: Qn
  not not_3 (not_3_out, d_ff_7_q);
  xnor xnor_2 (xnor_2_out, register_3_q, register_4_q);
  Register #(.width(1)) register_5 (.D(dipswitch_2_p3), .en(1'b1), .clk(clock_2_out), .Q(register_5_q), .clr(1'b0));
  J_K_Flip_Flop j_k_ff_7 (.J(in_1), .K(in_1), .clk(j_k_ff_3_qn), .Q(j_k_ff_1_q[2]));  // open: Qn, preset, reset
  and and_4 (and_4_out, d_ff_7_q, not_4_out);
  not not_4 (not_4_out, or_10_out);
  Register #(.width(1)) register_6 (.D(dipswitch_1_p3), .en(1'b1), .clk(clock_1_out), .Q(register_6_q), .clr(1'b0));
  and and_5 (and_5_out, xnor_2_out, xnor_1_out);
  Decoder #(.enable("false"), .select(3)) decoder_1 (
    .out0(decoder_1_out0), .out1(decoder_1_out1), .out2(decoder_1_out2), .out3(decoder_1_out3),
    .out4(decoder_1_out4), .out5(decoder_1_out5), .out6(decoder_1_out6), .out7(decoder_1_out7),
    .sel(j_k_ff_1_q));
  LED led_4 (.in(decoder_1_out7));
  LED led_5 (.in(decoder_1_out6));
  J_K_Flip_Flop j_k_ff_8 (
    .J(d_ff_3_q), .K(d_ff_3_q), .clk(d_ff_3_q), .Q(j_k_ff_8_q[0]), .Qn(j_k_ff_8_qn), .preset(button_10_out));  // open: reset
  and and_6 (and_6_out, xnor_4_out, xnor_5_out, xnor_7_out);
  J_K_Flip_Flop j_k_ff_9 (
    .J(and_9_out), .K(and_9_out), .clk(and_9_out), .Q(j_k_ff_9_q[0]), .Qn(j_k_ff_9_qn), .reset(or_5_out));  // open: preset
  Button button_1 ();  // open: out
  Button button_2 ();  // open: out
  Button button_3 ();  // open: out
  D_Flip_Flop #(.trigger("falling")) d_ff_8 (
    .D(d_ff_9_q), .clk(and_8_out), .Q(d_ff_8_q), .reset(not_5_out));  // open: Qn, preset
  not not_5 (not_5_out, d_ff_9_q);
  Button button_4 (.out(button_4_out));
  Button button_5 (.out(button_5_out));
  Register #(.width(1)) register_7 (.D(dipswitch_1_p4), .en(1'b1), .clk(clock_1_out), .Q(register_7_q), .clr(1'b0));
  xnor xnor_3 (xnor_3_out, register_6_q, register_5_q);
  Register #(.width(1)) register_8 (.D(dipswitch_2_p4), .en(1'b1), .clk(clock_2_out), .Q(register_8_q), .clr(1'b0));
  LED led_6 (.in(decoder_1_out5));
  LED led_7 (.in(decoder_1_out4));
  LED led_8 (.in(decoder_1_out3));
  J_K_Flip_Flop j_k_ff_10 (
    .J(d_ff_3_q), .K(d_ff_3_q), .clk(j_k_ff_8_qn), .Q(j_k_ff_8_q[1]), .Qn(j_k_ff_10_qn), .reset(button_10_out));  // open: preset
  J_K_Flip_Flop j_k_ff_11 (
    .J(and_9_out), .K(and_9_out), .clk(j_k_ff_9_qn), .Q(j_k_ff_9_q[1]), .Qn(j_k_ff_11_qn), .reset(or_5_out));  // open: preset
  Button button_6 ();  // open: out
  D_Flip_Flop d_ff_9 (.D(and_8_out), .clk(and_8_out), .Q(d_ff_9_q), .reset(d_ff_8_q));  // open: Qn, preset
  Button button_7 (.out(button_7_out));
  Button button_8 (.out(button_8_out));
  and and_7 (and_7_out, xnor_3_out, and_5_out);
  LED led_9 (.in(decoder_1_out2));
  LED led_10 (.in(decoder_1_out1));
  LED led_11 (.in(decoder_1_out0));
  xnor xnor_4 (xnor_4_out, j_k_ff_8_q[0], j_k_ff_9_q[0]);
  J_K_Flip_Flop j_k_ff_12 (
    .J(and_9_out), .K(and_9_out), .clk(j_k_ff_11_qn), .Q(j_k_ff_9_q[2]), .reset(or_5_out));  // open: Qn, preset
  or or_4 (or_4_out, button_7_out, button_8_out, button_5_out, button_4_out);
  and and_8 (and_8_out, not_1_out, or_4_out);
  and and_9 (and_9_out, d_ff_9_q, and_10_out);
  LED led_12 (.in(and_9_out));
  J_K_Flip_Flop j_k_ff_13 (
    .J(d_ff_3_q), .K(d_ff_3_q), .clk(j_k_ff_10_qn), .Q(j_k_ff_8_q[2]), .reset(button_10_out));  // open: Qn, preset
  xnor xnor_5 (xnor_5_out, j_k_ff_8_q[1], j_k_ff_9_q[1]);
  D_Flip_Flop d_ff_10 (
    .D(multiplexer_1_out), .clk(multiplexer_1_out), .Q(d_ff_10_q), .reset(d_ff_8_q));  // open: Qn, preset
  and and_10 (and_10_out, d_ff_9_q, d_ff_10_q);
  Hex_Digit_Display hex_digit_display_1 (.value({1'b0, j_k_ff_8_q}));  // open: dp
  xnor xnor_6 (xnor_6_out, register_7_q, register_8_q);
  xnor xnor_7 (xnor_7_out, j_k_ff_8_q[2], j_k_ff_9_q[2]);
  or or_5 (or_5_out, and_6_out, button_9_out);
  buf buffer_1 (buffer_1_out, and_10_out);
  not not_6 (not_6_out, buffer_1_out);
  and and_11 (and_11_out, d_ff_9_q, not_6_out);
  LED led_13 (.in(and_11_out));
  LED led_14 (.in(and_19_out));
  and and_12 (and_12_out, xnor_6_out, and_7_out);
  D_Flip_Flop d_ff_11 (.D(dipswitch_3_p1), .clk(decoder_1_out0), .Q(d_ff_11_q), .reset(1'b0));  // open: Qn, preset
  or or_6 (or_6_out, button_7_out, button_5_out);
  or or_7 (or_7_out, button_8_out, button_5_out);
  buf or_8 (or_8_out, button_4_out);  // OR_Gate
  and and_13 (and_13_out, and_2_out, multiplexer_10_out);
  LED led_15 (.in(and_13_out));
  LED led_16 (.in(and_18_out));
  LED led_17 (.in(and_12_out));
  D_Flip_Flop d_ff_12 (.D(dipswitch_3_p2), .clk(decoder_1_out0), .Q(d_ff_12_q), .reset(1'b0));  // open: Qn, preset
  LED led_18 (.in(and_17_out));
  // DipSwitch #(.number(4)) dipswitch_3: pin names not known; wires that end beside it: dipswitch_3_p1, dipswitch_3_p2, dipswitch_3_p3, dipswitch_3_p4, dipswitch_3_p5, dipswitch_3_p6, d_ff_12_q, d_ff_11_q
  buf buffer_2 (buffer_2_out, in_2);
  or or_9 (or_9_out, button_9_out, and_6_out);
  and and_14 (and_14_out, or_6_out, not_5_out);
  and and_15 (and_15_out, or_7_out, not_5_out);
  and and_16 (and_16_out, or_8_out, not_5_out);
  D_Flip_Flop d_ff_13 (.D(and_14_out), .clk(and_14_out), .Q(d_ff_13_q[0]), .reset(d_ff_8_q));  // open: Qn, preset
  Button button_9 (.out(button_9_out));
  and and_17 (and_17_out, and_2_out, multiplexer_11_out);
  D_Flip_Flop d_ff_14 (.D(dipswitch_3_p3), .clk(decoder_1_out0), .Q(dipswitch_3_p6), .reset(1'b0));  // open: Qn, preset
  buf buffer_3 (buffer_3_out, buffer_2_out);
  Button button_10 (.out(button_10_out));
  D_Flip_Flop d_ff_15 (.D(dipswitch_3_p4), .clk(decoder_1_out0), .Q(dipswitch_3_p5), .reset(1'b0));  // open: Qn, preset
  buf buffer_4 (buffer_4_out, buffer_3_out);
  D_Flip_Flop d_ff_16 (.D(and_15_out), .clk(and_15_out), .Q(d_ff_13_q[1]), .reset(d_ff_8_q));  // open: Qn, preset
  and and_18 (and_18_out, and_2_out, multiplexer_12_out);
  buf buffer_5 (buffer_5_out, buffer_4_out);
  buf buffer_6 (buffer_6_out, buffer_5_out);
  D_Flip_Flop d_ff_17 (.D(and_16_out), .clk(and_16_out), .Q(d_ff_13_q[2]), .reset(d_ff_8_q));  // open: Qn, preset
  buf buffer_7 (buffer_7_out, buffer_6_out);
  and and_19 (and_19_out, and_2_out, multiplexer_13_out);
  buf buffer_8 (buffer_8_out, buffer_7_out);
  Multiplexer #(.select(3)) multiplexer_1 (
    .in0(multiplexer_2_out), .in1(multiplexer_3_out), .in2(multiplexer_4_out), .in3(multiplexer_5_out),
    .in4(multiplexer_6_out), .in5(multiplexer_7_out), .in6(multiplexer_8_out), .in7(multiplexer_9_out),
    .out(multiplexer_1_out), .sel(j_k_ff_9_q));
  buf buffer_9 (buffer_9_out, buffer_8_out);
  buf buffer_10 (buffer_10_out, buffer_9_out);
  or or_10 (or_10_out, multiplexer_13_out, multiplexer_12_out, multiplexer_11_out, multiplexer_10_out);
  Multiplexer #(.select(3)) multiplexer_2 (
    .in0(1'b0), .in1(d_ff_18_q), .in2(d_ff_26_q), .in3(d_ff_34_q), .in4(d_ff_42_q), .out(multiplexer_2_out),
    .sel(d_ff_13_q));  // open: in5, in6, in7
  Multiplexer #(.select(3)) multiplexer_3 (
    .in0(1'b0), .in1(d_ff_19_q), .in2(d_ff_27_q), .in3(d_ff_35_q), .in4(d_ff_43_q), .out(multiplexer_3_out),
    .sel(d_ff_13_q));  // open: in5, in6, in7
  Multiplexer #(.select(3)) multiplexer_4 (
    .in0(1'b0), .in1(d_ff_20_q), .in2(d_ff_28_q), .in3(d_ff_36_q), .in4(d_ff_44_q), .out(multiplexer_4_out),
    .sel(d_ff_13_q));  // open: in5, in6, in7
  Multiplexer #(.select(3)) multiplexer_5 (
    .in0(1'b0), .in1(d_ff_21_q), .in2(d_ff_29_q), .in3(d_ff_37_q), .in4(d_ff_45_q), .out(multiplexer_5_out),
    .sel(d_ff_13_q));  // open: in5, in6, in7
  Multiplexer #(.select(3)) multiplexer_6 (
    .in0(1'b0), .in1(d_ff_22_q), .in2(d_ff_30_q), .in3(d_ff_38_q), .in4(d_ff_46_q), .out(multiplexer_6_out),
    .sel(d_ff_13_q));  // open: in5, in6, in7
  Multiplexer #(.select(3)) multiplexer_7 (
    .in0(1'b0), .in1(d_ff_23_q), .in2(d_ff_31_q), .in3(d_ff_39_q), .in4(d_ff_47_q), .out(multiplexer_7_out),
    .sel(d_ff_13_q));  // open: in5, in6, in7
  Multiplexer #(.select(3)) multiplexer_8 (
    .in0(1'b0), .in1(d_ff_24_q), .in2(d_ff_32_q), .in3(d_ff_40_q), .in4(d_ff_48_q), .out(multiplexer_8_out),
    .sel(d_ff_13_q));  // open: in5, in6, in7
  Multiplexer #(.select(3)) multiplexer_9 (
    .in0(1'b0), .in1(d_ff_25_q), .in2(d_ff_33_q), .in3(d_ff_41_q), .in4(d_ff_49_q), .out(multiplexer_9_out),
    .sel(d_ff_13_q));  // open: in5, in6, in7
  or or_11 (or_11_out, demultiplexer_1_out0, demultiplexer_1_out1, demultiplexer_1_out2, demultiplexer_1_out3);
  or or_12 (or_12_out, demultiplexer_2_out0, demultiplexer_2_out1, demultiplexer_2_out2, demultiplexer_2_out3);
  or or_13 (or_13_out, demultiplexer_3_out0, demultiplexer_3_out1, demultiplexer_3_out2, demultiplexer_3_out3);
  or or_14 (or_14_out, demultiplexer_4_out0, demultiplexer_4_out1, demultiplexer_4_out2, demultiplexer_4_out3);
  or or_15 (or_15_out, demultiplexer_5_out0, demultiplexer_5_out1, demultiplexer_5_out2, demultiplexer_5_out3);
  or or_16 (or_16_out, demultiplexer_6_out0, demultiplexer_6_out1, demultiplexer_6_out2, demultiplexer_6_out3);
  or or_17 (or_17_out, demultiplexer_7_out0, demultiplexer_7_out1, demultiplexer_7_out2, demultiplexer_7_out3);
  or or_18 (or_18_out, demultiplexer_8_out0, demultiplexer_8_out1, demultiplexer_8_out2, demultiplexer_8_out3);
  D_Flip_Flop d_ff_18 (
    .D(demultiplexer_1_out0), .clk(or_11_out), .Q(d_ff_18_q), .reset(button_10_out));  // open: Qn, preset
  D_Flip_Flop d_ff_19 (
    .D(demultiplexer_2_out0), .clk(or_12_out), .Q(d_ff_19_q), .reset(button_10_out));  // open: Qn, preset
  D_Flip_Flop d_ff_20 (
    .D(demultiplexer_3_out0), .clk(or_13_out), .Q(d_ff_20_q), .reset(button_10_out));  // open: Qn, preset
  D_Flip_Flop d_ff_21 (
    .D(demultiplexer_4_out0), .clk(or_14_out), .Q(d_ff_21_q), .reset(button_10_out));  // open: Qn, preset
  D_Flip_Flop d_ff_22 (
    .D(demultiplexer_5_out0), .clk(or_15_out), .Q(d_ff_22_q), .reset(button_10_out));  // open: Qn, preset
  D_Flip_Flop d_ff_23 (
    .D(demultiplexer_6_out0), .clk(or_16_out), .Q(d_ff_23_q), .reset(button_10_out));  // open: Qn, preset
  D_Flip_Flop d_ff_24 (
    .D(demultiplexer_7_out0), .clk(or_17_out), .Q(d_ff_24_q), .reset(button_10_out));  // open: Qn, preset
  D_Flip_Flop d_ff_25 (
    .D(demultiplexer_8_out0), .clk(or_18_out), .Q(d_ff_25_q), .reset(button_10_out));  // open: Qn, preset
  D_Flip_Flop d_ff_26 (
    .D(demultiplexer_1_out1), .clk(or_11_out), .Q(d_ff_26_q), .reset(button_10_out));  // open: Qn, preset
  D_Flip_Flop d_ff_27 (
    .D(demultiplexer_2_out1), .clk(or_12_out), .Q(d_ff_27_q), .reset(button_10_out));  // open: Qn, preset
  D_Flip_Flop d_ff_28 (
    .D(demultiplexer_3_out1), .clk(or_13_out), .Q(d_ff_28_q), .reset(button_10_out));  // open: Qn, preset
  D_Flip_Flop d_ff_29 (
    .D(demultiplexer_4_out1), .clk(or_14_out), .Q(d_ff_29_q), .reset(button_10_out));  // open: Qn, preset
  D_Flip_Flop d_ff_30 (
    .D(demultiplexer_5_out1), .clk(or_15_out), .Q(d_ff_30_q), .reset(button_10_out));  // open: Qn, preset
  D_Flip_Flop d_ff_31 (
    .D(demultiplexer_6_out1), .clk(or_16_out), .Q(d_ff_31_q), .reset(button_10_out));  // open: Qn, preset
  D_Flip_Flop d_ff_32 (
    .D(demultiplexer_7_out1), .clk(or_17_out), .Q(d_ff_32_q), .reset(button_10_out));  // open: Qn, preset
  D_Flip_Flop d_ff_33 (
    .D(demultiplexer_8_out1), .clk(or_18_out), .Q(d_ff_33_q), .reset(button_10_out));  // open: Qn, preset
  D_Flip_Flop d_ff_34 (
    .D(demultiplexer_1_out2), .clk(or_11_out), .Q(d_ff_34_q), .reset(button_10_out));  // open: Qn, preset
  D_Flip_Flop d_ff_35 (
    .D(demultiplexer_2_out2), .clk(or_12_out), .Q(d_ff_35_q), .reset(button_10_out));  // open: Qn, preset
  D_Flip_Flop d_ff_36 (
    .D(demultiplexer_3_out2), .clk(or_13_out), .Q(d_ff_36_q), .reset(button_10_out));  // open: Qn, preset
  D_Flip_Flop d_ff_37 (
    .D(demultiplexer_4_out2), .clk(or_14_out), .Q(d_ff_37_q), .reset(button_10_out));  // open: Qn, preset
  D_Flip_Flop d_ff_38 (
    .D(demultiplexer_5_out2), .clk(or_15_out), .Q(d_ff_38_q), .reset(button_10_out));  // open: Qn, preset
  D_Flip_Flop d_ff_39 (
    .D(demultiplexer_6_out2), .clk(or_16_out), .Q(d_ff_39_q), .reset(button_10_out));  // open: Qn, preset
  D_Flip_Flop d_ff_40 (
    .D(demultiplexer_7_out2), .clk(or_17_out), .Q(d_ff_40_q), .reset(button_10_out));  // open: Qn, preset
  D_Flip_Flop d_ff_41 (
    .D(demultiplexer_8_out2), .clk(or_18_out), .Q(d_ff_41_q), .reset(button_10_out));  // open: Qn, preset
  D_Flip_Flop d_ff_42 (
    .D(demultiplexer_1_out3), .clk(or_11_out), .Q(d_ff_42_q), .reset(button_10_out));  // open: Qn, preset
  D_Flip_Flop d_ff_43 (
    .D(demultiplexer_2_out3), .clk(or_12_out), .Q(d_ff_43_q), .reset(button_10_out));  // open: Qn, preset
  D_Flip_Flop d_ff_44 (
    .D(demultiplexer_3_out3), .clk(or_13_out), .Q(d_ff_44_q), .reset(button_10_out));  // open: Qn, preset
  D_Flip_Flop d_ff_45 (
    .D(demultiplexer_4_out3), .clk(or_14_out), .Q(d_ff_45_q), .reset(button_10_out));  // open: Qn, preset
  D_Flip_Flop d_ff_46 (
    .D(demultiplexer_5_out3), .clk(or_15_out), .Q(d_ff_46_q), .reset(button_10_out));  // open: Qn, preset
  D_Flip_Flop d_ff_47 (
    .D(demultiplexer_6_out3), .clk(or_16_out), .Q(d_ff_47_q), .reset(button_10_out));  // open: Qn, preset
  D_Flip_Flop d_ff_48 (
    .D(demultiplexer_7_out3), .clk(or_17_out), .Q(d_ff_48_q), .reset(button_10_out));  // open: Qn, preset
  D_Flip_Flop d_ff_49 (
    .D(demultiplexer_8_out3), .clk(or_18_out), .Q(d_ff_49_q), .reset(button_10_out));  // open: Qn, preset
  D_Flip_Flop d_ff_50 (.D(or_11_out), .clk(or_11_out), .Q(d_ff_50_q), .reset(button_10_out));  // open: Qn, preset
  Demultiplexer #(.select(2)) demultiplexer_1 (
    .out0(demultiplexer_1_out0), .out1(demultiplexer_1_out1), .out2(demultiplexer_1_out2),
    .out3(demultiplexer_1_out3), .in(and_20_out), .sel(random_1_out));
  Demultiplexer #(.select(2)) demultiplexer_2 (
    .out0(demultiplexer_2_out0), .out1(demultiplexer_2_out1), .out2(demultiplexer_2_out2),
    .out3(demultiplexer_2_out3), .in(demultiplexer_9_out1), .sel(random_1_out));
  Demultiplexer #(.select(2)) demultiplexer_3 (
    .out0(demultiplexer_3_out0), .out1(demultiplexer_3_out1), .out2(demultiplexer_3_out2),
    .out3(demultiplexer_3_out3), .in(demultiplexer_9_out2), .sel(random_1_out));
  Demultiplexer #(.select(2)) demultiplexer_4 (
    .out0(demultiplexer_4_out0), .out1(demultiplexer_4_out1), .out2(demultiplexer_4_out2),
    .out3(demultiplexer_4_out3), .in(demultiplexer_9_out3), .sel(random_1_out));
  Demultiplexer #(.select(2)) demultiplexer_5 (
    .out0(demultiplexer_5_out0), .out1(demultiplexer_5_out1), .out2(demultiplexer_5_out2),
    .out3(demultiplexer_5_out3), .in(demultiplexer_9_out4), .sel(random_1_out));
  Demultiplexer #(.select(2)) demultiplexer_6 (
    .out0(demultiplexer_6_out0), .out1(demultiplexer_6_out1), .out2(demultiplexer_6_out2),
    .out3(demultiplexer_6_out3), .in(demultiplexer_9_out5), .sel(random_1_out));
  Demultiplexer #(.select(2)) demultiplexer_7 (
    .out0(demultiplexer_7_out0), .out1(demultiplexer_7_out1), .out2(demultiplexer_7_out2),
    .out3(demultiplexer_7_out3), .in(demultiplexer_9_out6), .sel(random_1_out));
  Demultiplexer #(.select(2)) demultiplexer_8 (
    .out0(demultiplexer_8_out0), .out1(demultiplexer_8_out1), .out2(demultiplexer_8_out2),
    .out3(demultiplexer_8_out3), .in(demultiplexer_9_out7), .sel(random_1_out));
  and and_20 (and_20_out, demultiplexer_9_out0, not_7_out);
  not not_7 (not_7_out, d_ff_50_q);
  Multiplexer #(.select(3)) multiplexer_10 (
    .in0(d_ff_18_q), .in1(d_ff_19_q), .in2(d_ff_20_q), .in3(d_ff_21_q), .in4(d_ff_22_q), .in5(d_ff_23_q),
    .in6(d_ff_24_q), .in7(d_ff_25_q), .out(multiplexer_10_out), .sel(j_k_ff_2_q));
  Multiplexer #(.select(3)) multiplexer_11 (
    .in0(d_ff_26_q), .in1(d_ff_27_q), .in2(d_ff_28_q), .in3(d_ff_29_q), .in4(d_ff_30_q), .in5(d_ff_31_q),
    .in6(d_ff_32_q), .in7(d_ff_33_q), .out(multiplexer_11_out), .sel(j_k_ff_2_q));
  Multiplexer #(.select(3)) multiplexer_12 (
    .in0(d_ff_34_q), .in1(d_ff_35_q), .in2(d_ff_36_q), .in3(d_ff_37_q), .in4(d_ff_38_q), .in5(d_ff_39_q),
    .in6(d_ff_40_q), .in7(d_ff_41_q), .out(multiplexer_12_out), .sel(j_k_ff_2_q));
  Multiplexer #(.select(3)) multiplexer_13 (
    .in0(d_ff_42_q), .in1(d_ff_43_q), .in2(d_ff_44_q), .in3(d_ff_45_q), .in4(d_ff_46_q), .in5(d_ff_47_q),
    .in6(d_ff_48_q), .in7(d_ff_49_q), .out(multiplexer_13_out), .sel(j_k_ff_2_q));
  Demultiplexer #(.select(3)) demultiplexer_9 (
    .out0(demultiplexer_9_out0), .out1(demultiplexer_9_out1), .out2(demultiplexer_9_out2),
    .out3(demultiplexer_9_out3), .out4(demultiplexer_9_out4), .out5(demultiplexer_9_out5),
    .out6(demultiplexer_9_out6), .out7(demultiplexer_9_out7), .in(or_9_out), .sel(j_k_ff_9_q));
  Random #(.width(2)) random_1 (.next(or_9_out), .clk(or_9_out), .out(random_1_out));  // open: clr

  // Notes on the sheet:
  //   prevent some kids press all button,
  //   it wil count first pressed
  //   some delay before show 
  //   buffer? idk
  //   show until there is no data yet
  //   show all button that you must press
  //   4
  //   2
  //   1
  //   User
  //   Simon
  //   7
  //   6
  //   Correct
  //   5
  //   4
  //   3
  //   2
  //   1
  //   0
  //   compare if current state hit max
  //   current state
  //   Dont Forget to TURN ON Clock
  //   Max count
  //   Nah
  //   Start Game
  //   Reset Data
  //   prevent some kids press all button,
  //   it wil count first pressed
  //   Memory 4bits * 8 => 32 bits
  //   Random
endmodule
