// Logisim project simon_says_reduce.circ as structural Verilog: 1 circuit, main circuit main
// 3
module main (
);

  wire and_1_out, and_2_out, and_3_out, and_4_out, and_5_out, and_6_out, and_7_out, and_8_out, and_9_out,
       and_10_out, and_11_out, and_12_out, and_13_out, and_14_out, and_15_out, and_16_out, button_1_out,
       button_2_out, button_3_out, button_4_out, button_5_out, button_7_out, button_8_out, button_9_out,
       clock_1_out, clock_2_out, clock_3_out, d_ff_1_q, d_ff_2_q, d_ff_3_q, d_ff_4_q, d_ff_5_q, d_ff_6_q,
       d_ff_7_q, d_ff_8_q, d_ff_9_q, demultiplexer_9_out0, demultiplexer_9_out1, demultiplexer_9_out2,
       demultiplexer_9_out3, demultiplexer_9_out4, demultiplexer_9_out5, demultiplexer_9_out6,
       demultiplexer_9_out7, dipswitch_1_p1, dipswitch_1_p2, dipswitch_1_p3, dipswitch_1_p4, dipswitch_2_p1,
       dipswitch_2_p2, dipswitch_2_p3, dipswitch_2_p4, j_k_ff_1_qn, j_k_ff_2_qn, j_k_ff_3_q,
       multiplexer_1_out, multiplexer_2_out, multiplexer_3_out, multiplexer_4_out, multiplexer_5_out,
       multiplexer_6_out, multiplexer_7_out, multiplexer_8_out, multiplexer_9_out, multiplexer_10_out,
       multiplexer_11_out, multiplexer_12_out, multiplexer_13_out, not_1_out, not_2_out, not_3_out,
       not_4_out, not_5_out, not_6_out, or_1_out, or_2_out, or_3_out, or_4_out, or_5_out, or_6_out, or_9_out,
       or_10_out, or_11_out, or_12_out, or_13_out, or_14_out, or_15_out, or_16_out, or_17_out, or_18_out,
       or_19_out, register_1_q, register_2_q, register_3_q, register_4_q, register_5_q, register_6_q,
       register_7_q, register_8_q, xnor_1_out, xnor_2_out, xnor_3_out, xnor_4_out, xnor_5_out, xnor_6_out,
       xnor_7_out;
  wire [0:0] button_10_out;
  wire [1:0] random_1_out;
  wire [2:0] counter_1_q, counter_2_q, j_k_ff_1_q, or_7_out, register_9_q;
  wire [3:0] demultiplexer_1_out0, demultiplexer_2_out0, demultiplexer_3_out0, demultiplexer_4_out0,
       demultiplexer_5_out0, demultiplexer_6_out0, demultiplexer_7_out0, demultiplexer_8_out0, register_10_q,
       register_11_q, register_12_q, register_13_q, register_14_q, register_15_q, register_16_q,
       register_17_q;

  Clock clock_1 (.out(clock_1_out));
  Clock clock_2 (.out(clock_2_out));
  D_Flip_Flop d_ff_1 (.D(j_k_ff_3_q), .clk(j_k_ff_3_q), .Q(d_ff_1_q), .reset(and_4_out));  // open: Qn, preset
  Register #(.width(1)) register_1 (.D(dipswitch_1_p1), .en(1'b1), .clk(clock_1_out), .Q(register_1_q), .clr(1'b0));
  Register #(.width(1)) register_2 (.D(dipswitch_2_p1), .en(1'b1), .clk(clock_2_out), .Q(register_2_q), .clr(1'b0));
  or or_1 (or_1_out, and_6_out, button_9_out);
  not not_1 (not_1_out, d_ff_2_q);
  D_Flip_Flop d_ff_2 (.D(or_1_out), .clk(or_1_out), .Q(d_ff_2_q), .reset(and_4_out));  // open: Qn, preset
  and and_1 (and_1_out, d_ff_1_q, clock_3_out);
  or or_2 (or_2_out, or_1_out, button_9_out);
  and and_2 (and_2_out, d_ff_2_q, and_1_out);
  and and_3 (and_3_out, and_2_out, not_2_out);
  Clock clock_3 (.out(clock_3_out));
  // DipSwitch #(.number(4)) dipswitch_1: pin names not known; wires that end beside it: dipswitch_1_p1, dipswitch_1_p2, dipswitch_1_p3, dipswitch_1_p4
  // DipSwitch #(.number(4)) dipswitch_2: pin names not known; wires that end beside it: dipswitch_2_p1, dipswitch_2_p2, dipswitch_2_p3, dipswitch_2_p4
  J_K_Flip_Flop j_k_ff_1 (
    .J(and_2_out), .K(and_2_out), .clk(and_2_out), .Q(j_k_ff_1_q[0]), .Qn(j_k_ff_1_qn), .preset(or_1_out),
    .reset(and_4_out));
  D_Flip_Flop d_ff_3 (.D(and_3_out), .clk(and_3_out), .Q(d_ff_3_q), .reset(and_4_out));  // open: Qn, preset
  D_Flip_Flop d_ff_4 (.D(or_2_out), .clk(or_2_out), .Q(d_ff_4_q), .reset(and_4_out));  // open: Qn, preset
  Register #(.width(1)) register_3 (.D(dipswitch_1_p2), .en(1'b1), .clk(clock_1_out), .Q(register_3_q), .clr(1'b0));
  xnor xnor_1 (xnor_1_out, register_1_q, register_2_q);
  Register #(.width(1)) register_4 (.D(dipswitch_2_p2), .en(1'b1), .clk(clock_2_out), .Q(register_4_q), .clr(1'b0));
  J_K_Flip_Flop j_k_ff_2 (
    .J(and_2_out), .K(and_2_out), .clk(j_k_ff_1_qn), .Q(j_k_ff_1_q[1]), .Qn(j_k_ff_2_qn), .preset(or_1_out),
    .reset(and_4_out));
  D_Flip_Flop #(.trigger("falling")) d_ff_5 (
    .D(d_ff_3_q), .clk(and_3_out), .Q(d_ff_5_q), .reset(and_4_out));  // open: Qn, preset
  J_K_Flip_Flop #(.trigger("falling")) j_k_ff_3 (
    .J(d_ff_4_q), .K(d_ff_4_q), .clk(clock_3_out), .Q(j_k_ff_3_q), .reset(and_4_out));  // open: Qn, preset
  J_K_Flip_Flop j_k_ff_4 (
    .J(and_2_out), .K(and_2_out), .clk(j_k_ff_2_qn), .Q(j_k_ff_1_q[2]), .preset(or_1_out), .reset(and_4_out));  // open: Qn
  not not_2 (not_2_out, d_ff_5_q);
  xnor xnor_2 (xnor_2_out, register_3_q, register_4_q);
  Register #(.width(1)) register_5 (.D(dipswitch_2_p3), .en(1'b1), .clk(clock_2_out), .Q(register_5_q), .clr(1'b0));
  or or_3 (or_3_out, button_10_out[0], and_6_out);
  and and_4 (and_4_out, d_ff_5_q, not_3_out);
  not not_3 (not_3_out, or_10_out);
  Register #(.width(1)) register_6 (.D(dipswitch_1_p3), .en(1'b1), .clk(clock_1_out), .Q(register_6_q), .clr(1'b0));
  and and_5 (and_5_out, xnor_2_out, xnor_1_out);
  Counter #(.max('h7), .width(3)) counter_1 (
    .load(button_10_out[0]), .count(or_3_out), .clk(or_3_out), .D({2'b00, button_10_out[0]}), .Q(counter_1_q));  // open: clr, up, carry
  and and_6 (and_6_out, xnor_4_out, xnor_5_out, xnor_7_out);
  D_Flip_Flop d_ff_6 (.D(and_9_out), .clk(d_ff_8_q), .Q(d_ff_6_q), .reset(or_4_out));  // open: Qn, preset
  Counter #(.max('h7), .width(3)) counter_2 (
    .clr(or_6_out), .up(d_ff_6_q), .count(d_ff_6_q), .clk(d_ff_6_q), .Q(counter_2_q));  // open: load, D, carry
  Button button_1 (.out(button_1_out));
  Button button_2 (.out(button_2_out));
  Button button_3 (.out(button_3_out));
  or or_4 (or_4_out, d_ff_6_q, button_10_out[0]);
  Button button_4 (.out(button_4_out));
  Button button_5 (.out(button_5_out));
  Register #(.width(1)) register_7 (.D(dipswitch_1_p4), .en(1'b1), .clk(clock_1_out), .Q(register_7_q), .clr(1'b0));
  xnor xnor_3 (xnor_3_out, register_6_q, register_5_q);
  Register #(.width(1)) register_8 (.D(dipswitch_2_p4), .en(1'b1), .clk(clock_2_out), .Q(register_8_q), .clr(1'b0));
  Button button_6 (.out(or_7_out[2]));
  D_Flip_Flop d_ff_7 (.D(and_8_out), .clk(and_8_out), .Q(d_ff_7_q), .reset(or_4_out));  // open: Qn, preset
  Button button_7 (.out(button_7_out));
  Button button_8 (.out(button_8_out));
  and and_7 (and_7_out, xnor_3_out, and_5_out);
  xnor xnor_4 (xnor_4_out, counter_1_q[0], counter_2_q[0]);
  or or_5 (or_5_out, button_1_out, button_2_out, button_3_out, or_7_out[2]);
  and and_8 (and_8_out, not_1_out, or_5_out);
  D_Flip_Flop #(.trigger("falling")) d_ff_8 (
    .D(d_ff_7_q), .clk(and_8_out), .Q(d_ff_8_q), .reset(or_4_out));  // open: Qn, preset
  and and_9 (and_9_out, d_ff_7_q, and_10_out);
  LED led_1 (.in(and_9_out));
  xnor xnor_5 (xnor_5_out, counter_1_q[1], counter_2_q[1]);
  Hex_Digit_Display hex_digit_display_1 (.value({1'b0, counter_1_q}));  // open: dp
  xnor xnor_6 (xnor_6_out, register_7_q, register_8_q);
  or or_6 (or_6_out, and_6_out, button_9_out);
  D_Flip_Flop d_ff_9 (
    .D(multiplexer_1_out), .clk(multiplexer_1_out), .Q(d_ff_9_q), .reset(or_4_out));  // open: Qn, preset
  and and_10 (and_10_out, d_ff_7_q, d_ff_9_q);
  not not_4 (not_4_out, and_10_out);
  and and_11 (and_11_out, d_ff_7_q, not_4_out);
  LED led_2 (.in(and_11_out));
  LED led_3 (.in(and_16_out));
  and and_12 (and_12_out, xnor_6_out, and_7_out);
  xnor xnor_7 (xnor_7_out, counter_1_q[2], counter_2_q[2]);
  or or_7 (or_7_out[0], button_1_out, button_3_out);
  or or_8 (or_7_out[1], button_2_out, button_3_out);
  and and_13 (and_13_out, and_2_out, multiplexer_10_out);
  LED led_4 (.in(and_13_out));
  LED led_5 (.in(and_15_out));
  LED led_6 (.in(and_12_out));
  LED led_7 (.in(and_14_out));
  Button button_9 (.out(button_9_out));
  and and_14 (and_14_out, and_2_out, multiplexer_11_out);
  or or_9 (or_9_out, button_9_out, and_6_out);
  not not_5 (not_5_out, d_ff_7_q);
  Button button_10 (.out(button_10_out[0]));
  Register #(.width(3)) register_9 (.D(or_7_out), .en(not_5_out), .clk(or_5_out), .Q(register_9_q), .clr(or_4_out));
  and and_15 (and_15_out, and_2_out, multiplexer_12_out);
  and and_16 (and_16_out, and_2_out, multiplexer_13_out);
  Multiplexer #(.select(3)) multiplexer_1 (
    .in0(multiplexer_2_out), .in1(multiplexer_3_out), .in2(multiplexer_4_out), .in3(multiplexer_5_out),
    .in4(multiplexer_6_out), .in5(multiplexer_7_out), .in6(multiplexer_8_out), .in7(multiplexer_9_out),
    .out(multiplexer_1_out), .sel(counter_2_q));
  or or_10 (or_10_out, multiplexer_13_out, multiplexer_12_out, multiplexer_11_out, multiplexer_10_out);
  Multiplexer #(.select(3)) multiplexer_2 (
    .in0(1'b0), .in1(register_10_q[0]), .in2(register_10_q[1]), .in3(register_10_q[2]),
    .in4(register_10_q[3]), .out(multiplexer_2_out), .sel(register_9_q));  // open: in5, in6, in7
  Multiplexer #(.select(3)) multiplexer_3 (
    .in0(1'b0), .in1(register_11_q[0]), .in2(register_11_q[1]), .in3(register_11_q[2]),
    .in4(register_11_q[3]), .out(multiplexer_3_out), .sel(register_9_q));  // open: in5, in6, in7
  Multiplexer #(.select(3)) multiplexer_4 (
    .in0(1'b0), .in1(register_12_q[0]), .in2(register_12_q[1]), .in3(register_12_q[2]),
    .in4(register_12_q[3]), .out(multiplexer_4_out), .sel(register_9_q));  // open: in5, in6, in7
  Multiplexer #(.select(3)) multiplexer_5 (
    .in0(1'b0), .in1(register_13_q[0]), .in2(register_13_q[1]), .in3(register_13_q[2]),
    .in4(register_13_q[3]), .out(multiplexer_5_out), .sel(register_9_q));  // open: in5, in6, in7
  Multiplexer #(.select(3)) multiplexer_6 (
    .in0(1'b0), .in1(register_14_q[0]), .in2(register_14_q[1]), .in3(register_14_q[2]),
    .in4(register_14_q[3]), .out(multiplexer_6_out), .sel(register_9_q));  // open: in5, in6, in7
  Multiplexer #(.select(3)) multiplexer_7 (
    .in0(1'b0), .in1(register_15_q[0]), .in2(register_15_q[1]), .in3(register_15_q[2]),
    .in4(register_15_q[3]), .out(multiplexer_7_out), .sel(register_9_q));  // open: in5, in6, in7
  Multiplexer #(.select(3)) multiplexer_8 (
    .in0(1'b0), .in1(register_16_q[0]), .in2(register_16_q[1]), .in3(register_16_q[2]),
    .in4(register_16_q[3]), .out(multiplexer_8_out), .sel(register_9_q));  // open: in5, in6, in7
  Multiplexer #(.select(3)) multiplexer_9 (
    .in0(1'b0), .in1(register_17_q[0]), .in2(register_17_q[1]), .in3(register_17_q[2]),
    .in4(register_17_q[3]), .out(multiplexer_9_out), .sel(register_9_q));  // open: in5, in6, in7
  or or_11 (or_11_out, register_10_q[3], register_10_q[2], register_10_q[1], register_10_q[0]);
  or or_12 (or_12_out, demultiplexer_1_out0[0], demultiplexer_1_out0[1], demultiplexer_1_out0[2], demultiplexer_1_out0[3]);
  not not_6 (not_6_out, or_11_out);
  or or_13 (or_13_out, demultiplexer_2_out0[0], demultiplexer_2_out0[1], demultiplexer_2_out0[2], demultiplexer_2_out0[3]);
  or or_14 (or_14_out, demultiplexer_3_out0[0], demultiplexer_3_out0[1], demultiplexer_3_out0[2], demultiplexer_3_out0[3]);
  or or_15 (or_15_out, demultiplexer_4_out0[0], demultiplexer_4_out0[1], demultiplexer_4_out0[2], demultiplexer_4_out0[3]);
  or or_16 (or_16_out, demultiplexer_5_out0[0], demultiplexer_5_out0[1], demultiplexer_5_out0[2], demultiplexer_5_out0[3]);
  or or_17 (or_17_out, demultiplexer_6_out0[0], demultiplexer_6_out0[1], demultiplexer_6_out0[2], demultiplexer_6_out0[3]);
  or or_18 (or_18_out, demultiplexer_7_out0[0], demultiplexer_7_out0[1], demultiplexer_7_out0[2], demultiplexer_7_out0[3]);
  or or_19 (or_19_out, demultiplexer_8_out0[0], demultiplexer_8_out0[1], demultiplexer_8_out0[2], demultiplexer_8_out0[3]);
  Register #(.width(4)) register_10 (
    .D(demultiplexer_1_out0), .en(not_6_out), .clk(or_12_out), .Q(register_10_q), .clr(button_10_out[0]));
  Register #(.width(4)) register_11 (
    .D(demultiplexer_2_out0), .en(or_13_out), .clk(or_13_out), .Q(register_11_q), .clr(button_10_out[0]));
  Register #(.width(4)) register_12 (
    .D(demultiplexer_3_out0), .en(or_14_out), .clk(or_14_out), .Q(register_12_q), .clr(button_10_out[0]));
  Register #(.width(4)) register_13 (
    .D(demultiplexer_4_out0), .en(or_15_out), .clk(or_15_out), .Q(register_13_q), .clr(button_10_out[0]));
  Register #(.width(4)) register_14 (
    .D(demultiplexer_5_out0), .en(or_16_out), .clk(or_16_out), .Q(register_14_q), .clr(button_10_out[0]));
  Register #(.width(4)) register_15 (
    .D(demultiplexer_6_out0), .en(or_17_out), .clk(or_17_out), .Q(register_15_q), .clr(button_10_out[0]));
  Register #(.width(4)) register_16 (
    .D(demultiplexer_7_out0), .en(or_18_out), .clk(or_18_out), .Q(register_16_q), .clr(button_10_out[0]));
  Register #(.width(4)) register_17 (
    .D(demultiplexer_8_out0), .en(or_19_out), .clk(or_19_out), .Q(register_17_q), .clr(button_10_out[0]));
  Demultiplexer #(.select(2)) demultiplexer_1 (
    .out0(demultiplexer_1_out0[0]), .out1(demultiplexer_1_out0[1]), .out2(demultiplexer_1_out0[2]),
    .out3(demultiplexer_1_out0[3]), .in(demultiplexer_9_out0), .sel(random_1_out));
  Demultiplexer #(.select(2)) demultiplexer_2 (
    .out0(demultiplexer_2_out0[0]), .out1(demultiplexer_2_out0[1]), .out2(demultiplexer_2_out0[2]),
    .out3(demultiplexer_2_out0[3]), .in(demultiplexer_9_out1), .sel(random_1_out));
  Demultiplexer #(.select(2)) demultiplexer_3 (
    .out0(demultiplexer_3_out0[0]), .out1(demultiplexer_3_out0[1]), .out2(demultiplexer_3_out0[2]),
    .out3(demultiplexer_3_out0[3]), .in(demultiplexer_9_out2), .sel(random_1_out));
  Demultiplexer #(.select(2)) demultiplexer_4 (
    .out0(demultiplexer_4_out0[0]), .out1(demultiplexer_4_out0[1]), .out2(demultiplexer_4_out0[2]),
    .out3(demultiplexer_4_out0[3]), .in(demultiplexer_9_out3), .sel(random_1_out));
  Demultiplexer #(.select(2)) demultiplexer_5 (
    .out0(demultiplexer_5_out0[0]), .out1(demultiplexer_5_out0[1]), .out2(demultiplexer_5_out0[2]),
    .out3(demultiplexer_5_out0[3]), .in(demultiplexer_9_out4), .sel(random_1_out));
  Demultiplexer #(.select(2)) demultiplexer_6 (
    .out0(demultiplexer_6_out0[0]), .out1(demultiplexer_6_out0[1]), .out2(demultiplexer_6_out0[2]),
    .out3(demultiplexer_6_out0[3]), .in(demultiplexer_9_out5), .sel(random_1_out));
  Demultiplexer #(.select(2)) demultiplexer_7 (
    .out0(demultiplexer_7_out0[0]), .out1(demultiplexer_7_out0[1]), .out2(demultiplexer_7_out0[2]),
    .out3(demultiplexer_7_out0[3]), .in(demultiplexer_9_out6), .sel(random_1_out));
  Demultiplexer #(.select(2)) demultiplexer_8 (
    .out0(demultiplexer_8_out0[0]), .out1(demultiplexer_8_out0[1]), .out2(demultiplexer_8_out0[2]),
    .out3(demultiplexer_8_out0[3]), .in(demultiplexer_9_out7), .sel(random_1_out));
  Multiplexer #(.select(3)) multiplexer_10 (
    .in0(register_10_q[0]), .in1(register_11_q[0]), .in2(register_12_q[0]), .in3(register_13_q[0]),
    .in4(register_14_q[0]), .in5(register_15_q[0]), .in6(register_16_q[0]), .in7(register_17_q[0]),
    .out(multiplexer_10_out), .sel(j_k_ff_1_q));
  Multiplexer #(.select(3)) multiplexer_11 (
    .in0(register_10_q[1]), .in1(register_11_q[1]), .in2(register_12_q[1]), .in3(register_13_q[1]),
    .in4(register_14_q[1]), .in5(register_15_q[1]), .in6(register_16_q[1]), .in7(register_17_q[1]),
    .out(multiplexer_11_out), .sel(j_k_ff_1_q));
  Multiplexer #(.select(3)) multiplexer_12 (
    .in0(register_10_q[2]), .in1(register_11_q[2]), .in2(register_12_q[2]), .in3(register_13_q[2]),
    .in4(register_14_q[2]), .in5(register_15_q[2]), .in6(register_16_q[2]), .in7(register_17_q[2]),
    .out(multiplexer_12_out), .sel(j_k_ff_1_q));
  Multiplexer #(.select(3)) multiplexer_13 (
    .in0(register_10_q[3]), .in1(register_11_q[3]), .in2(register_12_q[3]), .in3(register_13_q[3]),
    .in4(register_14_q[3]), .in5(register_15_q[3]), .in6(register_16_q[3]), .in7(register_17_q[3]),
    .out(multiplexer_13_out), .sel(j_k_ff_1_q));
  Random #(.width(2)) random_1 (.next(or_9_out), .clk(or_9_out), .out(random_1_out));  // open: clr
  Demultiplexer #(.select(3)) demultiplexer_9 (
    .out0(demultiplexer_9_out0), .out1(demultiplexer_9_out1), .out2(demultiplexer_9_out2),
    .out3(demultiplexer_9_out3), .out4(demultiplexer_9_out4), .out5(demultiplexer_9_out5),
    .out6(demultiplexer_9_out6), .out7(demultiplexer_9_out7), .in(or_9_out), .sel(counter_2_q));

  // Notes on the sheet:
  //   some delay before show 
  //   show until there is no data yet
  //   show all button that you must press
  //   User
  //   Simon
  //   it wil count first pressed
  //   prevent some kids press all button,
  //   current state
  //   Dont Forget to TURN ON Clock
  //   Max count
  //   Nah
  //   Start Game
  //   Reset Data
  //   compare if current state hit max
  //   Memory 4bits * 8 => 32 bits
  //   Random
endmodule
