// Logisim project simon_says_reduce_5.circ as structural Verilog
// 3
module main (
);

  wire and_1_out, and_2_out, and_3_out, button_6_out, button_7_out, button_8_out, clock_1_out, clock_2_out,
       demultiplexer_6_out0, demultiplexer_6_out1, demultiplexer_6_out2, demultiplexer_6_out3,
       demultiplexer_6_out4, demultiplexer_6_out5, demultiplexer_6_out6, demultiplexer_6_out7,
       dipswitch_1_p1, dipswitch_1_p2, dipswitch_1_p3, dipswitch_1_p4, dipswitch_2_p1, dipswitch_2_p2,
       dipswitch_2_p3, dipswitch_2_p4, multiplexer_2_out, multiplexer_3_out, multiplexer_4_out,
       multiplexer_5_out, multiplexer_6_out, n7400_1_pin3, n7400_1_pin6, n7404_1_pin5, n7404_1_pin6,
       n7404_2_pin5, n7404_3_pin1, n7404_4_pin8, n7408_1_pin1, n7408_1_pin2, n7408_1_pin3, n7408_1_pin4,
       n7408_1_pin5, n7408_1_pin6, n7408_2_pin12, n7408_3_pin12, n7408_4_pin2, n7408_4_pin3, n7408_4_pin12,
       n7408_5_pin2, n7408_5_pin3, n7408_5_pin4, n7408_5_pin6, n7408_5_pin8, n7408_5_pin10, n7408_5_pin11,
       n7408_5_pin13, n7411_1_pin3, n7411_1_pin4, n7411_1_pin5, n7432_1_pin11, n7432_1_pin12, n7432_1_pin13,
       n7432_2_pin5, n7432_2_pin8, n7432_2_pin9, n7432_3_pin3, n7432_4_pin11, n7432_4_pin12, n7432_5_pin8,
       n7432_5_pin11, n7474_1_pin1, n7474_2_pin2, n7474_3_pin2, n7474_3_pin3, n7474_3_pin5, n7474_4_pin2,
       n7474_4_pin3, n7474_5_pin1, n7474_5_pin2, n7474_5_pin3, n7474_5_pin9, n7474_5_pin12, n7474_6_pin2,
       n7474_6_pin3, n7474_6_pin12, n7486_1_pin3, n7486_1_pin6, n7486_1_pin11, not_1_out, or_3_out, or_4_out,
       or_5_out, or_6_out, or_7_out, or_8_out, register_1_q, register_2_q, register_3_q, register_4_q,
       register_5_q, register_6_q, register_7_q, register_8_q, undriven, undriven_2, undriven_3, xnor_1_out,
       xnor_2_out, xnor_3_out, xnor_4_out;
  wire [0:0] n7432_2_pin10;
  wire [1:0] random_1_out;
  wire [2:0] counter_1_q, counter_2_q, counter_3_q, n7432_5_pin3, register_9_q;
  wire [3:0] demultiplexer_1_out0, demultiplexer_2_out0, demultiplexer_3_out0, demultiplexer_4_out0,
       demultiplexer_5_out0, register_10_q, register_11_q, register_12_q, register_13_q, register_14_q;

  Clock clock_1 (.out(clock_1_out));
  Clock clock_2 (.out(clock_2_out));
  Register #(.width(1)) register_1 (.D(dipswitch_1_p1), .en(1'b1), .clk(clock_1_out), .Q(register_1_q), .clr(1'b0));
  Register #(.width(1)) register_2 (.D(dipswitch_2_p1), .en(1'b1), .clk(clock_2_out), .Q(register_2_q), .clr(1'b0));
  _7432 u_7432_1 (
    .pin13(n7432_1_pin13), .pin12(n7432_1_pin12), .pin11(n7432_1_pin11));  // open: pin1, pin2, pin3, pin4, pin5, pin6, pin10, pin9, pin8
  // DipSwitch #(.number(4)) dipswitch_1: pin names not known; wires that end beside it: dipswitch_1_p1, dipswitch_1_p2, dipswitch_1_p3, dipswitch_1_p4
  // DipSwitch #(.number(4)) dipswitch_2: pin names not known; wires that end beside it: dipswitch_2_p1, dipswitch_2_p2, dipswitch_2_p3, dipswitch_2_p4
  _7432 u_7432_2 (
    .pin4(n7432_1_pin12), .pin5(n7432_2_pin5), .pin6(n7432_1_pin13), .pin10(n7432_2_pin10[0]),
    .pin9(n7432_2_pin9), .pin8(n7432_2_pin8));  // open: pin1, pin2, pin3, pin13, pin12, pin11
  _7404 u_7404_1 (
    .pin5(n7404_1_pin5), .pin6(n7404_1_pin6));  // open: pin1, pin2, pin3, pin4, pin13, pin12, pin11, pin10, pin9, pin8
  _7474 u_7474_1 (
    .pin1(n7474_1_pin1), .pin2(n7432_1_pin13), .pin3(n7432_1_pin13), .pin5(n7404_1_pin5));  // open: pin4, pin6, pin13, pin12, pin11, pin10, pin9, pin8
  _7408 u_7408_1 (
    .pin1(n7408_1_pin1), .pin2(n7408_1_pin2), .pin3(n7408_1_pin3), .pin4(n7408_1_pin4), .pin5(n7408_1_pin5),
    .pin6(n7408_1_pin6), .pin10(n7404_1_pin5), .pin9(n7408_1_pin3), .pin8(n7408_1_pin4));  // open: pin13, pin12, pin11
  _7474 u_7474_2 (
    .pin1(n7474_1_pin1), .pin2(n7474_2_pin2), .pin3(n7474_2_pin2), .pin5(n7408_1_pin1));  // open: pin4, pin6, pin13, pin12, pin11, pin10, pin9, pin8
  Register #(.width(1)) register_3 (.D(dipswitch_1_p2), .en(1'b1), .clk(clock_1_out), .Q(register_3_q), .clr(1'b0));
  xnor xnor_1 (xnor_1_out, register_1_q, register_2_q);
  Register #(.width(1)) register_4 (.D(dipswitch_2_p2), .en(1'b1), .clk(clock_2_out), .Q(register_4_q), .clr(1'b0));
  _7432 u_7432_3 (
    .pin1(n7408_1_pin4), .pin2(n7432_1_pin13), .pin3(n7432_3_pin3));  // open: pin4, pin5, pin6, pin13, pin12, pin11, pin10, pin9, pin8
  Clock clock_3 (.out(n7408_1_pin2));
  xnor xnor_2 (xnor_2_out, register_3_q, register_4_q);
  Register #(.width(1)) register_5 (.D(dipswitch_2_p3), .en(1'b1), .clk(clock_2_out), .Q(register_5_q), .clr(1'b0));
  _7400 u_7400_1 (
    .pin1(n7432_2_pin10[0]), .pin2(n7432_2_pin10[0]), .pin3(n7400_1_pin3), .pin4(n7400_1_pin3),
    .pin5(n7432_2_pin5), .pin6(n7400_1_pin6), .pin10(n7400_1_pin6), .pin9(n7400_1_pin6), .pin8(n7432_2_pin9));  // open: pin13, pin12, pin11
  _7474 u_7474_3 (
    .pin1(n7474_1_pin1), .pin2(n7474_3_pin2), .pin3(n7474_3_pin3), .pin5(n7474_3_pin5), .pin13(n7474_1_pin1),
    .pin12(n7408_1_pin6), .pin11(n7408_1_pin6), .pin9(n7474_3_pin2));  // open: pin4, pin6, pin10, pin8
  _7474 u_7474_4 (
    .pin1(n7474_1_pin1), .pin2(n7474_4_pin2), .pin3(n7474_4_pin3), .pin5(n7474_2_pin2), .pin13(n7474_1_pin1),
    .pin12(n7432_1_pin11), .pin11(n7432_1_pin11), .pin9(n7474_4_pin2));  // open: pin4, pin6, pin10, pin8
  Register #(.width(1)) register_6 (.D(dipswitch_1_p3), .en(1'b1), .clk(clock_1_out), .Q(register_6_q), .clr(1'b0));
  and and_1 (and_1_out, xnor_2_out, xnor_1_out);
  Counter #(.max('h7), .width(3)) counter_1 (
    .clr(n7404_2_pin5), .load(n7432_1_pin13), .count(n7432_3_pin3), .clk(n7432_3_pin3), .Q(counter_1_q));  // open: up, D, carry
  _7404 u_7404_2 (
    .pin1(n7474_3_pin5), .pin2(n7408_1_pin5), .pin3(n7408_1_pin2), .pin4(n7474_4_pin3), .pin5(n7404_2_pin5),
    .pin6(n7474_1_pin1), .pin13(n7408_1_pin6), .pin12(n7474_3_pin3));  // open: pin11, pin10, pin9, pin8
  Register #(.width(1)) register_7 (.D(dipswitch_1_p4), .en(1'b1), .clk(clock_1_out), .Q(register_7_q), .clr(1'b0));
  xnor xnor_3 (xnor_3_out, register_6_q, register_5_q);
  Register #(.width(1)) register_8 (.D(dipswitch_2_p4), .en(1'b1), .clk(clock_2_out), .Q(register_8_q), .clr(1'b0));
  _7411 u_7411_1 (
    .pin3(n7411_1_pin3), .pin4(n7411_1_pin4), .pin5(n7411_1_pin5), .pin6(n7432_2_pin5));  // open: pin1, pin2, pin13, pin12, pin11, pin10, pin9, pin8
  and and_2 (and_2_out, xnor_3_out, and_1_out);
  Counter #(.max('h7), .width(3)) counter_2 (
    .load(n7432_2_pin10[0]), .count(n7432_2_pin8), .clk(n7432_2_pin8), .D({2'b00, n7432_2_pin10[0]}),
    .Q(counter_2_q));  // open: clr, up, carry
  _7432 u_7432_4 (
    .pin13(n7432_2_pin10[0]), .pin12(n7432_4_pin12), .pin11(n7432_4_pin11));  // open: pin1, pin2, pin3, pin4, pin5, pin6, pin10, pin9, pin8
  _7474 u_7474_5 (
    .pin1(n7474_5_pin1), .pin2(n7474_5_pin2), .pin3(n7474_5_pin3), .pin5(n7432_4_pin12),
    .pin13(n7474_5_pin1), .pin12(n7474_5_pin12), .pin11(n7474_5_pin12), .pin9(n7474_5_pin9));  // open: pin4, pin6, pin10, pin8
  Button button_1 ();  // open: out
  Button button_2 ();  // open: out
  _7474 u_7474_6 (
    .pin1(n7474_5_pin1), .pin2(n7474_6_pin2), .pin3(n7474_6_pin3), .pin5(n7474_5_pin3), .pin13(n7474_5_pin1),
    .pin12(n7474_6_pin12), .pin11(n7474_6_pin12), .pin9(n7474_6_pin2));  // open: pin4, pin6, pin10, pin8
  Button button_3 (.out(n7432_5_pin3[2]));
  _7408 u_7408_2 (
    .pin13(n7474_3_pin5), .pin12(n7408_2_pin12), .pin11(n7404_2_pin5));  // open: pin1, pin2, pin3, pin4, pin5, pin6, pin10, pin9, pin8
  _7404 u_7404_3 (
    .pin1(n7404_3_pin1), .pin2(n7408_2_pin12));  // open: pin3, pin4, pin5, pin6, pin13, pin12, pin11, pin10, pin9, pin8
  xnor xnor_4 (xnor_4_out, register_7_q, register_8_q);
  Counter #(.max('h7), .width(3)) counter_3 (
    .clr(n7432_5_pin8), .up(n7432_4_pin12), .count(n7432_4_pin12), .clk(n7432_4_pin12), .Q(counter_3_q));  // open: load, D, carry
  Button button_4 ();  // open: out
  Button button_5 ();  // open: out
  _7408 u_7408_3 (
    .pin13(n7404_1_pin6), .pin12(n7408_3_pin12), .pin11(n7474_6_pin12));  // open: pin1, pin2, pin3, pin4, pin5, pin6, pin10, pin9, pin8
  Button button_6 (.out(button_6_out));
  Button button_7 (.out(button_7_out));
  and and_3 (and_3_out, xnor_4_out, and_2_out);
  _7408 u_7408_4 (
    .pin1(n7474_6_pin2), .pin2(n7408_4_pin2), .pin3(n7408_4_pin3), .pin13(n7474_6_pin2),
    .pin12(n7408_4_pin12), .pin11(n7474_5_pin2), .pin10(n7474_6_pin2), .pin9(n7474_5_pin9),
    .pin8(n7408_4_pin12));  // open: pin4, pin5, pin6
  LED led_1 (.in(n7474_5_pin2));
  Button button_8 (.out(button_8_out));
  LED led_2 (.in(and_3_out));
  or or_1 (n7408_3_pin12, button_6_out, button_8_out, button_7_out, n7432_5_pin3[2]);
  Hex_Digit_Display hex_digit_display_1 (.value({1'b0, counter_2_q}));  // open: dp
  _7404 u_7404_4 (
    .pin1(n7408_4_pin12), .pin2(n7408_4_pin2), .pin13(n7432_4_pin11), .pin12(n7474_5_pin1),
    .pin11(n7474_6_pin12), .pin10(n7474_6_pin3), .pin9(n7474_6_pin2), .pin8(n7404_4_pin8));  // open: pin3, pin4, pin5, pin6
  LED led_3 (.in(n7408_4_pin3));
  LED led_4 (.in(n7408_5_pin8));
  _7486 u_7486_1 (
    .pin1(counter_2_q[1]), .pin2(counter_3_q[1]), .pin3(n7486_1_pin3), .pin4(counter_3_q[2]),
    .pin5(counter_2_q[2]), .pin6(n7486_1_pin6), .pin13(counter_2_q[0]), .pin12(counter_3_q[0]),
    .pin11(n7486_1_pin11));  // open: pin10, pin9, pin8
  _7404 u_7404_5 (
    .pin5(n7486_1_pin3), .pin6(n7411_1_pin4), .pin11(n7486_1_pin11), .pin10(n7411_1_pin5),
    .pin9(n7486_1_pin6), .pin8(n7411_1_pin3));  // open: pin1, pin2, pin3, pin4, pin13, pin12
  LED led_5 (.in(n7408_5_pin3));
  LED led_6 (.in(n7408_5_pin11));
  LED led_7 (.in(n7408_5_pin6));
  _7432 u_7432_5 (
    .pin1(button_6_out), .pin2(button_7_out), .pin3(n7432_5_pin3[0]), .pin4(button_8_out),
    .pin5(button_7_out), .pin6(n7432_5_pin3[1]), .pin13(n7432_1_pin12), .pin12(n7432_2_pin9),
    .pin11(n7432_5_pin11), .pin10(n7432_2_pin5), .pin9(n7432_1_pin12), .pin8(n7432_5_pin8));
  Button button_9 (.out(n7432_1_pin12));
  _7408 u_7408_5 (
    .pin1(n7408_1_pin4), .pin2(n7408_5_pin2), .pin3(n7408_5_pin3), .pin4(n7408_5_pin4), .pin5(n7408_1_pin4),
    .pin6(n7408_5_pin6), .pin13(n7408_5_pin13), .pin12(n7408_1_pin4), .pin11(n7408_5_pin11),
    .pin10(n7408_5_pin10), .pin9(n7408_1_pin4), .pin8(n7408_5_pin8));
  Register #(.width(3)) register_9 (
    .D(n7432_5_pin3), .en(n7404_4_pin8), .clk(n7408_3_pin12), .Q(register_9_q), .clr(n7432_4_pin11));
  Button button_10 (.out(n7432_2_pin10[0]));
  Multiplexer #(.select(3)) multiplexer_1 (
    .in0(multiplexer_2_out), .in1(multiplexer_3_out), .in2(multiplexer_4_out), .in3(multiplexer_5_out),
    .in4(multiplexer_6_out), .in5(undriven), .in6(undriven_2), .in7(undriven_3), .out(n7474_5_pin12),
    .sel(counter_3_q));
  or or_2 (n7404_3_pin1, n7408_5_pin10, n7408_5_pin13, n7408_5_pin4, n7408_5_pin2);
  // DIP_74151 dip_74151_1: pin names not known
  Multiplexer #(.select(3)) multiplexer_2 (
    .in0(1'b0), .in1(register_10_q[0]), .in2(register_10_q[1]), .in3(register_10_q[2]),
    .in4(register_10_q[3]), .out(multiplexer_2_out), .sel(register_9_q));  // open: in5, in6, in7
  Multiplexer #(.select(3)) multiplexer_3 (
    .in0(1'b0), .in1(register_11_q[0]), .in2(register_11_q[1]), .in3(register_11_q[2]),
    .in4(register_11_q[3]), .out(multiplexer_3_out), .sel(register_9_q));  // open: in5, in6, in7
  Multiplexer #(.select(3)) multiplexer_4 (
    .in0(1'b0), .in1(register_12_q[0]), .in2(register_12_q[1]), .in3(register_12_q[2]),
    .in4(register_12_q[3]), .out(multiplexer_4_out), .sel(register_9_q));  // open: in5, in6, in7
  Multiplexer #(.select(3)) multiplexer_5 (
    .in0(1'b0), .in1(register_13_q[0]), .in2(register_13_q[1]), .in3(register_13_q[2]),
    .in4(register_13_q[3]), .out(multiplexer_5_out), .sel(register_9_q));  // open: in5, in6, in7
  Multiplexer #(.select(3)) multiplexer_6 (
    .in0(1'b0), .in1(register_14_q[0]), .in2(register_14_q[1]), .in3(register_14_q[2]),
    .in4(register_14_q[3]), .out(multiplexer_6_out), .sel(register_9_q));  // open: in5, in6, in7
  or or_3 (or_3_out, demultiplexer_1_out0[0], demultiplexer_1_out0[1], demultiplexer_1_out0[2], demultiplexer_1_out0[3]);
  or or_4 (or_4_out, register_10_q[3], register_10_q[2], register_10_q[1], register_10_q[0]);
  or or_5 (or_5_out, demultiplexer_2_out0[0], demultiplexer_2_out0[1], demultiplexer_2_out0[2], demultiplexer_2_out0[3]);
  or or_6 (or_6_out, demultiplexer_3_out0[0], demultiplexer_3_out0[1], demultiplexer_3_out0[2], demultiplexer_3_out0[3]);
  or or_7 (or_7_out, demultiplexer_4_out0[0], demultiplexer_4_out0[1], demultiplexer_4_out0[2], demultiplexer_4_out0[3]);
  or or_8 (or_8_out, demultiplexer_5_out0[0], demultiplexer_5_out0[1], demultiplexer_5_out0[2], demultiplexer_5_out0[3]);
  not not_1 (not_1_out, or_4_out);
  Register #(.width(4)) register_10 (
    .D(demultiplexer_1_out0), .en(not_1_out), .clk(or_3_out), .Q(register_10_q), .clr(n7432_2_pin10[0]));
  Register #(.width(4)) register_11 (
    .D(demultiplexer_2_out0), .en(or_5_out), .clk(or_5_out), .Q(register_11_q), .clr(n7432_2_pin10[0]));
  Register #(.width(4)) register_12 (
    .D(demultiplexer_3_out0), .en(or_6_out), .clk(or_6_out), .Q(register_12_q), .clr(n7432_2_pin10[0]));
  Register #(.width(4)) register_13 (
    .D(demultiplexer_4_out0), .en(or_7_out), .clk(or_7_out), .Q(register_13_q), .clr(n7432_2_pin10[0]));
  Register #(.width(4)) register_14 (
    .D(demultiplexer_5_out0), .en(or_8_out), .clk(or_8_out), .Q(register_14_q), .clr(n7432_2_pin10[0]));
  Demultiplexer #(.select(2)) demultiplexer_1 (
    .out0(demultiplexer_1_out0[0]), .out1(demultiplexer_1_out0[1]), .out2(demultiplexer_1_out0[2]),
    .out3(demultiplexer_1_out0[3]), .in(demultiplexer_6_out0), .sel(random_1_out));
  Demultiplexer #(.select(2)) demultiplexer_2 (
    .out0(demultiplexer_2_out0[0]), .out1(demultiplexer_2_out0[1]), .out2(demultiplexer_2_out0[2]),
    .out3(demultiplexer_2_out0[3]), .in(demultiplexer_6_out1), .sel(random_1_out));
  Demultiplexer #(.select(2)) demultiplexer_3 (
    .out0(demultiplexer_3_out0[0]), .out1(demultiplexer_3_out0[1]), .out2(demultiplexer_3_out0[2]),
    .out3(demultiplexer_3_out0[3]), .in(demultiplexer_6_out2), .sel(random_1_out));
  Demultiplexer #(.select(2)) demultiplexer_4 (
    .out0(demultiplexer_4_out0[0]), .out1(demultiplexer_4_out0[1]), .out2(demultiplexer_4_out0[2]),
    .out3(demultiplexer_4_out0[3]), .in(demultiplexer_6_out3), .sel(random_1_out));
  Demultiplexer #(.select(2)) demultiplexer_5 (
    .out0(demultiplexer_5_out0[0]), .out1(demultiplexer_5_out0[1]), .out2(demultiplexer_5_out0[2]),
    .out3(demultiplexer_5_out0[3]), .in(demultiplexer_6_out4), .sel(random_1_out));
  Multiplexer #(.select(3)) multiplexer_7 (
    .in0(register_10_q[0]), .in1(register_11_q[0]), .in2(register_12_q[0]), .in3(register_13_q[0]),
    .in4(register_14_q[0]), .out(n7408_5_pin2), .sel(counter_1_q));  // open: in5, in6, in7
  Multiplexer #(.select(3)) multiplexer_8 (
    .in0(register_10_q[1]), .in1(register_11_q[1]), .in2(register_12_q[1]), .in3(register_13_q[1]),
    .in4(register_14_q[1]), .out(n7408_5_pin4), .sel(counter_1_q));  // open: in5, in6, in7
  Multiplexer #(.select(3)) multiplexer_9 (
    .in0(register_10_q[2]), .in1(register_11_q[2]), .in2(register_12_q[2]), .in3(register_13_q[2]),
    .in4(register_14_q[2]), .out(n7408_5_pin13), .sel(counter_1_q));  // open: in5, in6, in7
  Multiplexer #(.select(3)) multiplexer_10 (
    .in0(register_10_q[3]), .in1(register_11_q[3]), .in2(register_12_q[3]), .in3(register_13_q[3]),
    .in4(register_14_q[3]), .out(n7408_5_pin10), .sel(counter_1_q));  // open: in5, in6, in7
  Random #(.width(2)) random_1 (.next(n7432_5_pin11), .clk(n7432_5_pin11), .out(random_1_out));  // open: clr
  Demultiplexer #(.select(3)) demultiplexer_6 (
    .out0(demultiplexer_6_out0), .out1(demultiplexer_6_out1), .out2(demultiplexer_6_out2),
    .out3(demultiplexer_6_out3), .out4(demultiplexer_6_out4), .out5(demultiplexer_6_out5),
    .out6(demultiplexer_6_out6), .out7(demultiplexer_6_out7), .in(n7432_5_pin11), .sel(counter_3_q));

  // Notes on the sheet:
  //   User
  //   some delay before show 
  //   show all button that you must press
  //   Simon
  //   this is counter (ic)
  //   show until there is no data yet
  //   Max count
  //   will go next state if release button
  //   correct
  //   compare if current state hit max
  //   current state
  //   Dont Forget to TURN ON Clock
  //   it wil count first pressed
  //   prevent some kids press all button,
  //   still do nothing if you press wrong button
  //   give me idea plz faii, im depressed
  //   Start Game
  //   Nah
  //   Reset Data
  //   Memory 4bits * 8 => 32 bits
  //   Random
endmodule
